// Logisim project cpu.circ as structural Verilog
module ALU_Input_Stage (
  input  Zero,
  input  Negate,
  input  [7:0] Input,
  output [7:0] Output
);

  wire not_1_out, not_2_out;
  wire [7:0] controlled_buffer_1_out;

  not not_1 (not_1_out, Zero);
  assign controlled_buffer_1_out = not_1_out ? Input : 8'bz;  // Controlled_Buffer controlled_buffer_1
  assign controlled_buffer_1_out = Zero ? {8{1'b0}} : 8'bz;  // Controlled_Buffer controlled_buffer_2
  not not_2 (not_2_out, Negate);
  assign Output = not_2_out ? controlled_buffer_1_out : 8'bz;  // Controlled_Buffer controlled_buffer_3
  assign Output = Negate ? ~controlled_buffer_1_out : 8'bz;  // Controlled_Inverter controlled_inverter_1
endmodule

module ALU_Output_Stage (
  input  OE,
  input  Inverted_OE,
  input  [7:0] Input,
  output [7:0] Output
);

  assign Output = OE ? Input : 8'bz;  // Controlled_Buffer controlled_buffer_1
  assign Output = Inverted_OE ? ~Input : 8'bz;  // Controlled_Inverter controlled_inverter_1
endmodule

module ALU_Operation_Stage (
  input  Carry_In,
  input  [1:0] Carry_Select,
  input  [1:0] Operation_Select,
  input  [7:0] Left_Input,
  input  [7:0] Right_Input,
  output [7:0] Output,
  output Carry_Out,
  output Negative_Out,
  output Zero_Out
);

  wire adder_1_cout, decoder_1_out0, decoder_1_out1, decoder_1_out2, decoder_1_out3, multiplexer_1_out,
       right_shifter_1_carry_in_2;
  wire [7:0] adder_1_out, and_1_out, right_shifter_1_output, xor_1_out;

  Adder adder_1 (.a(Left_Input), .b(Right_Input), .out(adder_1_out), .cin(multiplexer_1_out), .cout(adder_1_cout));
  assign and_1_out = Left_Input & Right_Input;  // AND_Gate and_1, 8 bits wide
  assign xor_1_out = Left_Input ^ Right_Input;  // XOR_Gate xor_1, 8 bits wide
  Right_Shifter right_shifter_1 (
    .Input(Left_Input), .Output(right_shifter_1_output), .Carry_In(multiplexer_1_out),
    .Carry_In_2(right_shifter_1_carry_in_2));
  Multiplexer #(.select(2), .enable("false")) multiplexer_1 (
    .in0(1'b0), .in1(1'b1), .in2(Carry_In), .out(multiplexer_1_out), .sel(Carry_Select));  // open: in3
  Multiplexer #(.select(2), .enable("false")) multiplexer_2 (
    .in0(adder_1_cout), .in1(1'b0), .in2(1'b0), .in3(right_shifter_1_carry_in_2), .out(Carry_Out),
    .sel(Operation_Select));
  assign {Negative_Out, Output[6:0]} = decoder_1_out0 ? adder_1_out : 8'bz;  // Controlled_Buffer controlled_buffer_1
  assign {Negative_Out, Output[6:0]} = decoder_1_out1 ? and_1_out : 8'bz;  // Controlled_Buffer controlled_buffer_2
  Decoder #(.select(2), .disabled(0), .enable("false")) decoder_1 (
    .out0(decoder_1_out0), .out1(decoder_1_out1), .out2(decoder_1_out2), .out3(decoder_1_out3),
    .sel(Operation_Select));
  assign {Negative_Out, Output[6:0]} = decoder_1_out2 ? xor_1_out : 8'bz;  // Controlled_Buffer controlled_buffer_3
  assign {Negative_Out, Output[6:0]} = decoder_1_out3 ? right_shifter_1_output : 8'bz;  // Controlled_Buffer controlled_buffer_4
  nor nor_1 (Zero_Out, Negative_Out, Output[6], Output[5], Output[4], Output[3], Output[2], Output[1], Output[0]);

  assign Output[7] = Negative_Out;
endmodule

module Right_Shifter (
  input  Carry_In,
  input  [7:0] Input,
  output [7:0] Output,
  output Carry_In_2
);


  assign Carry_In_2 = Input[0];
  assign Output = {Carry_In, Input[7:1]};
endmodule

module ALU (
  input  Zero_Left,
  input  Negate_Left,
  input  Zero_Right,
  input  Negate_Right,
  input  Carry_In,
  input  [1:0] Carry_Select,
  input  [1:0] Operation_Select,
  input  Output,
  input  Inverted_Output,
  input  [7:0] Left_Input,
  input  [7:0] Right_Input,
  output [7:0] Output_2,
  output Carry_Out,
  output Negative_Out,
  output Zero_Out
);

  wire [7:0] Left_Input_Stage_output, Operation_Stage_output, Right_Input_Stage_output;

  ALU_Input_Stage Left_Input_Stage (
    .Input(Left_Input), .Output(Left_Input_Stage_output), .Zero(Zero_Left), .Negate(Negate_Left));
  ALU_Input_Stage Right_Input_Stage (
    .Input(Right_Input), .Output(Right_Input_Stage_output), .Zero(Zero_Right), .Negate(Negate_Right));
  ALU_Operation_Stage Operation_Stage (
    .Left_Input(Left_Input_Stage_output), .Right_Input(Right_Input_Stage_output),
    .Output(Operation_Stage_output), .Carry_In(Carry_In), .Carry_Select(Carry_Select),
    .Operation_Select(Operation_Select), .Carry_Out(Carry_Out), .Negative_Out(Negative_Out),
    .Zero_Out(Zero_Out));
  ALU_Output_Stage Output_Stage (
    .Input(Operation_Stage_output), .Output(Output_2), .OE(Output), .Inverted_OE(Inverted_Output));
endmodule
